// Logisim project final simulation XD.circ as structural Verilog: 7 circuits, main circuit FullAdder
module FullAdder (
  input  cin1,
  input  cin2,
  input  cin3,
  output sum,
  output carry
);

  wire and_1_out, and_2_out, xor_1_out, xor_2_out;

  xor xor_1 (xor_1_out, cin1, cin2);
  xor xor_2 (xor_2_out, cin2, cin1);
  and and_1 (and_1_out, cin2, cin1);
  xor xor_3 (sum, xor_1_out, cin3);
  and and_2 (and_2_out, xor_2_out, cin3);
  or or_1 (carry, and_2_out, and_1_out);
endmodule

module \and  (
  input  cin1,
  input  cin2,
  output cout
);

  and and_1 (cout, cin1, cin2);
endmodule

module sign (
  input  sign1,
  input  sign_2,
  output sign_out
);

  xor xor_1 (sign_out, sign1, sign_2);
endmodule

module mult (
  input  fa0,
  input  fa1,
  input  A0,
  input  A1,
  input  A2,
  input  fBo,
  input  Bo,
  input  B1,
  output fo,
  output f1,
  output f2,
  output c0,
  output c1,
  output c2,
  output c3,
  output c4
);

  wire and_1_cout, and_3_cout, and_4_cout, and_5_cout, and_6_cout, and_7_cout, and_8_cout, and_9_cout,
       and_10_cout, and_11_cout, and_12_cout, and_13_cout, and_14_cout, and_15_cout, fulladder_1_carry,
       fulladder_1_sum, fulladder_2_carry, fulladder_3_carry, fulladder_3_sum, fulladder_4_carry,
       fulladder_4_sum, fulladder_5_carry, fulladder_6_carry, fulladder_7_carry, fulladder_8_carry,
       fulladder_8_sum, fulladder_9_carry;

  \and  and_1 (.cin1(B1), .cin2(A2), .cout(and_1_cout));
  \and  and_2 (.cin1(fa0), .cin2(fBo), .cout(fo));
  \and  and_3 (.cin1(A1), .cin2(fBo), .cout(and_3_cout));
  \and  and_4 (.cin1(A2), .cin2(fBo), .cout(and_4_cout));
  \and  and_5 (.cin1(Bo), .cin2(A1), .cout(and_5_cout));
  \and  and_6 (.cin1(B1), .cin2(A0), .cout(and_6_cout));
  \and  and_7 (.cin1(Bo), .cin2(A2), .cout(and_7_cout));
  \and  and_8 (.cin1(A1), .cin2(B1), .cout(and_8_cout));
  \and  and_9 (.cin1(fa1), .cin2(fBo), .cout(and_9_cout));
  \and  and_10 (.cin1(A0), .cin2(fBo), .cout(and_10_cout));
  \and  and_11 (.cin1(A0), .cin2(Bo), .cout(and_11_cout));
  \and  and_12 (.cin1(fa1), .cin2(B1), .cout(and_12_cout));
  FullAdder fulladder_1 (
    .cin1(and_4_cout), .cin2(and_5_cout), .cin3(and_6_cout), .sum(fulladder_1_sum), .carry(fulladder_1_carry));
  \and  and_13 (.cin1(fa1), .cin2(Bo), .cout(and_13_cout));
  \and  and_14 (.cin1(fa0), .cin2(Bo), .cout(and_14_cout));
  FullAdder fulladder_2 (.cin1(1'b0), .cin2(and_14_cout), .cin3(and_9_cout), .sum(f1), .carry(fulladder_2_carry));
  FullAdder fulladder_3 (
    .cin1(and_10_cout), .cin2(and_15_cout), .cin3(and_13_cout), .sum(fulladder_3_sum),
    .carry(fulladder_3_carry));
  \and  and_15 (.cin1(fa0), .cin2(B1), .cout(and_15_cout));
  FullAdder fulladder_4 (
    .cin1(and_3_cout), .cin2(and_11_cout), .cin3(and_12_cout), .sum(fulladder_4_sum),
    .carry(fulladder_4_carry));
  FullAdder fulladder_5 (
    .cin1(fulladder_2_carry), .cin2(fulladder_3_sum), .cin3(1'b0), .sum(f2), .carry(fulladder_5_carry));
  FullAdder fulladder_6 (
    .cin1(fulladder_5_carry), .cin2(fulladder_3_carry), .cin3(fulladder_4_sum), .sum(c0),
    .carry(fulladder_6_carry));
  FullAdder fulladder_7 (
    .cin1(fulladder_6_carry), .cin2(fulladder_4_carry), .cin3(fulladder_1_sum), .sum(c1),
    .carry(fulladder_7_carry));
  FullAdder fulladder_8 (
    .cin1(fulladder_7_carry), .cin2(fulladder_1_carry), .cin3(1'b0), .sum(fulladder_8_sum),
    .carry(fulladder_8_carry));
  FullAdder fulladder_9 (
    .cin1(fulladder_8_sum), .cin2(and_7_cout), .cin3(and_8_cout), .sum(c2), .carry(fulladder_9_carry));
  FullAdder fulladder_10 (.cin1(fulladder_9_carry), .cin2(and_1_cout), .cin3(fulladder_8_carry), .sum(c3), .carry(c4));
endmodule

module Final_Calc (
  input  FA1,
  input  FA0,
  input  A0,
  input  A1,
  input  A2,
  input  FB0,
  input  B1,
  input  B2,
  input  sign_A,
  input  sign_B
);

  wire dec_to_bcd_1_d0, dec_to_bcd_1_d1, dec_to_bcd_1_d2, dec_to_bcd_1_d3, int_to_bcd_t0, int_to_bcd_t1,
       int_to_bcd_u0, int_to_bcd_u1, int_to_bcd_u2, int_to_bcd_u3, mult_1_c0, mult_1_c1, mult_1_c2,
       mult_1_c3, mult_1_c4, mult_1_f1, mult_1_f2, mult_1_fo, n7_segment_display_driver_1_p5,
       n7_segment_display_driver_1_p6, n7_segment_display_driver_1_p7, n7_segment_display_driver_1_p8,
       n7_segment_display_driver_1_p9, n7_segment_display_driver_1_p10, n7_segment_display_driver_1_p11,
       n7_segment_display_driver_2_p5, n7_segment_display_driver_2_p6, n7_segment_display_driver_2_p7,
       n7_segment_display_driver_2_p8, n7_segment_display_driver_2_p9, n7_segment_display_driver_2_p10,
       n7_segment_display_driver_2_p11, n7_segment_display_driver_3_p5, n7_segment_display_driver_3_p6,
       n7_segment_display_driver_3_p7, n7_segment_display_driver_3_p8, n7_segment_display_driver_3_p9,
       n7_segment_display_driver_3_p10, n7_segment_display_driver_3_p11, n7_segment_display_driver_3_p12,
       not_1_out, or_1_out, sign_1_sign_out;

  mult mult_1 (
    .fa0(FA1), .fa1(FA0), .A0(A0), .A1(A1), .A2(A2), .fBo(FB0), .Bo(B1), .B1(B2), .fo(mult_1_fo),
    .f1(mult_1_f1), .f2(mult_1_f2), .c0(mult_1_c0), .c1(mult_1_c1), .c2(mult_1_c2), .c3(mult_1_c3),
    .c4(mult_1_c4));
  Dec_to_bcd dec_to_bcd_1 (
    .f0(mult_1_f2), .f1(mult_1_f1), .f2(mult_1_fo), .d0(dec_to_bcd_1_d0), .d1(dec_to_bcd_1_d1),
    .d2(dec_to_bcd_1_d2), .d3(dec_to_bcd_1_d3));
  int_to_bcd int_to_bcd (
    .c0(mult_1_c0), .c1(mult_1_c1), .c2(mult_1_c2), .c3(mult_1_c3), .c4(mult_1_c4), .u0(int_to_bcd_u0),
    .u1(int_to_bcd_u1), .u2(int_to_bcd_u2), .u3(int_to_bcd_u3), .t0(int_to_bcd_t0), .t1(int_to_bcd_t1));
  sign sign_1 (.sign1(sign_A), .sign_2(sign_B), .sign_out(sign_1_sign_out));
  // _7_segment_display_driver 7_segment_display_driver_1: pin names not known; wires that end beside it: dec_to_bcd_1_d3, dec_to_bcd_1_d2, dec_to_bcd_1_d1, dec_to_bcd_1_d0, n7_segment_display_driver_1_p5, n7_segment_display_driver_1_p6, n7_segment_display_driver_1_p7, n7_segment_display_driver_1_p8, n7_segment_display_driver_1_p9, n7_segment_display_driver_1_p10, n7_segment_display_driver_1_p11
  // _7_segment_display_driver 7_segment_display_driver_2: pin names not known; wires that end beside it: 1'b0, 1'b0, int_to_bcd_t1, int_to_bcd_t0, n7_segment_display_driver_2_p5, n7_segment_display_driver_2_p6, n7_segment_display_driver_2_p7, n7_segment_display_driver_2_p8, n7_segment_display_driver_2_p9, n7_segment_display_driver_2_p10, n7_segment_display_driver_2_p11
  // _7_segment_display_driver 7_segment_display_driver_3: pin names not known; wires that end beside it: int_to_bcd_u3, int_to_bcd_u2, int_to_bcd_u1, int_to_bcd_u0, n7_segment_display_driver_3_p5, n7_segment_display_driver_3_p6, n7_segment_display_driver_3_p7, n7_segment_display_driver_3_p8, n7_segment_display_driver_3_p9, n7_segment_display_driver_3_p10, n7_segment_display_driver_3_p11, n7_segment_display_driver_3_p12, n7_segment_display_driver_3_p12
  or or_1 (or_1_out, FB0, B1, B2, A2, A1, A0, FA0, FA1);
  not not_1 (not_1_out, or_1_out);
  _7_Segment_Display u_7_segment_display_1 (
    .g(n7_segment_display_driver_2_p11), .f(n7_segment_display_driver_2_p10),
    .a(n7_segment_display_driver_2_p5), .b(n7_segment_display_driver_2_p6),
    .e(n7_segment_display_driver_2_p9), .d(n7_segment_display_driver_2_p8),
    .c(n7_segment_display_driver_2_p7), .dp(1'b0));
  LED led_1 (.in(sign_1_sign_out));
  _7_Segment_Display u_7_segment_display_2 (
    .g(n7_segment_display_driver_3_p11), .f(n7_segment_display_driver_3_p10),
    .a(n7_segment_display_driver_3_p5), .b(n7_segment_display_driver_3_p6),
    .e(n7_segment_display_driver_3_p9), .d(n7_segment_display_driver_3_p8),
    .c(n7_segment_display_driver_3_p7), .dp(1'b1));
  _7_Segment_Display u_7_segment_display_3 (
    .g(n7_segment_display_driver_1_p11), .f(n7_segment_display_driver_1_p10),
    .a(n7_segment_display_driver_1_p5), .b(n7_segment_display_driver_1_p6),
    .e(n7_segment_display_driver_1_p9), .d(n7_segment_display_driver_1_p8), .c(n7_segment_display_driver_1_p7));  // open: dp
  LED led_2 (.in(not_1_out));

  // Notes on the sheet:
  //   Mult
  //   Dec to bcd
  //   sign flag
  //   zero flag
endmodule

module Dec_to_bcd (
  input  f0,
  input  f1,
  input  f2,
  output d0,
  output d1,
  output d2,
  output d3
);

  wire and_1_out, and_2_out, and_3_out, and_5_out, not_1_out, not_2_out, not_3_out;

  not not_1 (not_1_out, f0);
  not not_2 (not_2_out, f1);
  not not_3 (not_3_out, f2);
  and and_1 (and_1_out, f2, f1, not_1_out);
  xor xor_1 (d0, f0, f1, f2);
  and and_2 (and_2_out, f0, f2, not_2_out);
  and and_3 (and_3_out, not_2_out, f0);
  and and_4 (d3, f1, f0);
  and and_5 (and_5_out, not_1_out, f1, not_3_out);
  or or_1 (d2, and_3_out, and_1_out);
  or or_2 (d1, and_2_out, and_5_out);
endmodule

module int_to_bcd (
  input  c0,
  input  c1,
  input  c2,
  input  c3,
  input  c4,
  output u0,
  output u1,
  output u2,
  output u3,
  output t0,
  output t1
);

  wire and_1_out, and_2_out, and_3_out, and_4_out, and_5_out, and_6_out, and_7_out, and_8_out, and_9_out,
       c1_bar_out, c2_bar_out, c3_bar_out, c4_bar_out, or_1_out, or_2_out, or_3_out, or_4_out, or_6_out,
       xor_1_out, xor_2_out;

  not c3_bar (c3_bar_out, c3);
  not c2_bar (c2_bar_out, c2);
  not c4_bar (c4_bar_out, c4);
  not c1_bar (c1_bar_out, c1);
  xor xor_1 (xor_1_out, c1, c3_bar_out);
  and and_1 (and_1_out, c2_bar_out, xor_1_out, c4);
  or or_1 (or_1_out, c2, c4_bar_out);
  or or_2 (or_2_out, c1, c3_bar_out);
  or or_3 (or_3_out, c1_bar_out, c3);
  and and_2 (and_2_out, c1, c3_bar_out, or_1_out);
  and and_3 (and_3_out, c4_bar_out, c1_bar_out, c2, c3);
  and and_4 (and_4_out, c2, c4_bar_out, or_2_out);
  and and_5 (and_5_out, c2_bar_out, c4, or_3_out);
  and and_6 (and_6_out, c1_bar_out, c4_bar_out, c3);
  and and_7 (and_7_out, c1, c3_bar_out, c4);
  or or_4 (or_4_out, c1, c2);
  or or_5 (u2, and_4_out, and_5_out);
  or or_6 (or_6_out, and_6_out, and_7_out);
  or or_7 (u1, and_1_out, and_2_out, and_3_out);
  and and_8 (and_8_out, c2_bar_out, c3_bar_out, c4);
  and and_9 (and_9_out, c4_bar_out, c3, or_4_out);
  xor xor_2 (xor_2_out, c2, c3);
  and and_10 (u3, c2_bar_out, or_6_out);
  or or_8 (t0, and_8_out, and_9_out);
  and and_11 (t1, c4, xor_2_out);

  assign u0 = c0;

  // Notes on the sheet:
  //   c3 bar
endmodule
